# Fritzing sketch piezo (saved by Fritzing 0.9.3b)
breadboards: 1

parts:
  Part1 = Arduino Uno (Rev3) - ICSP
  R1 = Resistor [tolerance=±1% resistance=1k package=THT]
  Q1 = NPN-Transistor [package="TO92 [THT]"]
  R2 = Resistor [tolerance=±1% resistance=1k package=THT]
  J1 = Piezo Speaker
  VCC1 = Battery block 9V

nets:
  N1: Part1.GND, Q1.E, VCC1.-
  N2: Part1.D3_PWM, R1.Pin_1
  N3: R1.Pin_0, Q1.B
  N4: Q1.C, R2.Pin_1, J1.pin1
  N5: R2.Pin_0, J1.pin2, VCC1.+

notes:
  We used an NPN Transistor PN2222 for this build. If you're using a transistor for a similar build, make sure you consider the order of the Base, Collector, and Emitter pins. The Base pin should receive its signal from Arduino Pin #3, the Collector pin should connect to the Piezo buzzer and its resistor, and the Emitter pin should connect to Ground.
